// Logisim project BB-8.circ as structural Verilog: 5 circuits, main circuit main
module main (
);

  wire ALU_ACC, and_1_out, and_2_out, and_4_out, CLK, clock_1_out, comparator_1_eq, comparator_2_eq,
       comparator_3_eq, comparator_4_eq, comparator_5_eq, comparator_6_eq, EXT_0, EXT_1, EXT_MEM_CLK,
       EXT_MEM_PRO, FLG_CAR, FLG_EQU, FLG_GRE, FLG_LES, FLG_ZER, IF_RES, INC_PC, key_manager_1_clr,
       key_manager_1_con, key_manager_1_rd, keyboard_1_avail, nand_1_out, NIT, not_1_out, not_2_out,
       not_3_out, not_4_out, not_6_out, not_7_out, not_8_out, not_9_out, not_10_out, or_1_out, or_2_out,
       or_5_out, or_6_out, or_7_out, PC_HI_ACC, PC_LO_ACC, PRT_A_B, PRT_B_B, PRT_BC_SEL, PRT_C_B, PRT_D_B,
       pull_resistor_1_node, pull_resistor_5_node, pull_resistor_6_node, REG_ALU, REG_DIP, REG_EN, REG_MEM,
       REG_PC_HI, REG_PC_LO, REG_SHI, regs_1_wrt, REQ_IF, RST, SYS, telnet_1_p5, ttl_manager_1_ttl_en,
       ttl_manager_1_ttl_rst, undriven;
  wire [3:0] MCC_OP, multiplexer_2_out, rom_1_data;
  wire [6:0] keyboard_1_data, ttl_manager_1_ttl_dat;
  wire [7:0] ACC, ALU, controlled_buffer_5_out, DIP, dipswitch_1_sw8, dipswitch_2_sw8, EXT_MEM_OPCODE,
       EXT_MEM_OPERAND, MEM, multiplexer_7_out, PRT_C, PRT_D, ram_1_dout, ram_2_dout, random_1_out,
       register_1_q, register_2_q, register_3_q, rom_2_data, SHI, telnet_1_p4;
  wire [7:7] PC_HI;
  wire [9:0] counter_1_q, multiplexer_1_out;
  wire [14:0] MEM15;
  wire [15:0] multiplexer_5_out;

  // Probe on multiplexer_1_out
  Multiplexer #(.width(10)) multiplexer_1 (
    .in0({10{1'b1}}), .in1({MEM, 2'b00}), .out(multiplexer_1_out), .sel(not_1_out));
  not not_1 (not_1_out, RST);
  or or_1 (or_1_out, RST, NIT);
  Counter #(.max('h3ff), .width(10)) counter_1 (
    .load(or_1_out), .D(multiplexer_1_out), .count(1'b1), .Q(counter_1_q), .up(1'b1), .clk(CLK));  // open: carry, clr
  Pull_Resistor pull_resistor_1 (.node(pull_resistor_1_node));
  assign pull_resistor_1_node = PRT_BC_SEL ? CLK : 1'bz;  // Controlled_Buffer controlled_buffer_1
  ROM #(.addrWidth(10)) rom_1 (.addr(counter_1_q), .data({MCC_OP, rom_1_data}));
  // Probe on telnet_1_p4
  // Probe on ACC
  // Telnet #(.port(8080)) telnet_1: pin names not known; wires that end beside it: ACC, pull_resistor_1_node, PRT_B_B, telnet_1_p4, telnet_1_p5, PRT_C_B
  Comparator #(.mode("unsigned"), .width(4)) comparator_1 (
    .a(MCC_OP), .b(4'b0001), .eq(comparator_1_eq));  // open: gt, lt
  assign PRT_C = PRT_BC_SEL ? telnet_1_p4 : 8'bz;  // Controlled_Buffer controlled_buffer_2
  assign EXT_0 = PRT_BC_SEL ? telnet_1_p5 : 1'bz;  // Controlled_Buffer controlled_buffer_3
  and and_1 (and_1_out, rom_1_data[0], rom_1_data[1], rom_1_data[2], rom_1_data[3], MCC_OP[0], MCC_OP[1], MCC_OP[2], MCC_OP[3]);
  Clock clock_1 (.out(clock_1_out));
  Pull_Resistor pull_resistor_2 (.node(CLK));
  assign CLK = or_2_out ? clock_1_out : 1'bz;  // Controlled_Buffer controlled_buffer_4
  or or_2 (or_2_out, nand_1_out, RST);
  nand nand_1 (nand_1_out, comparator_1_eq, SYS);
  or or_3 (NIT, IF_RES, and_1_out);
  Decoder #(.select(4)) decoder_1 (
    .out0(REG_MEM), .out1(PC_HI_ACC), .out2(PC_LO_ACC), .out3(INC_PC), .out4(REG_PC_HI), .out5(REG_PC_LO),
    .out6(REG_DIP), .out7(REG_ALU), .out8(ALU_ACC), .out9(REQ_IF), .out10(PRT_A_B), .out11(REG_SHI),
    .out12(PRT_B_B), .out13(PRT_C_B), .out14(PRT_D_B), .out15(SYS), .sel(rom_1_data));  // open: en
  or or_4 (REG_EN, REG_MEM, REG_PC_HI, REG_PC_LO, REG_DIP, REG_ALU, REG_SHI, PRT_C_B, PRT_D_B);
  assign controlled_buffer_5_out = REG_MEM ? MEM : 8'bz;  // Controlled_Buffer controlled_buffer_5
  assign controlled_buffer_5_out = REG_PC_LO ? MEM15[7:0] : 8'bz;  // Controlled_Buffer controlled_buffer_6
  assign controlled_buffer_5_out = REG_PC_HI ? {PC_HI[7], MEM15[14:8]} : 8'bz;  // Controlled_Buffer controlled_buffer_7
  assign controlled_buffer_5_out = REG_DIP ? DIP : 8'bz;  // Controlled_Buffer controlled_buffer_8
  assign controlled_buffer_5_out = REG_ALU ? ALU : 8'bz;  // Controlled_Buffer controlled_buffer_9
  assign controlled_buffer_5_out = REG_SHI ? SHI : 8'bz;  // Controlled_Buffer controlled_buffer_10
  assign controlled_buffer_5_out = PRT_C_B ? PRT_C : 8'bz;  // Controlled_Buffer controlled_buffer_11
  assign controlled_buffer_5_out = PRT_D_B ? PRT_D : 8'bz;  // Controlled_Buffer controlled_buffer_12
  not not_2 (not_2_out, FLG_ZER);
  not not_3 (not_3_out, FLG_CAR);
  not not_4 (not_4_out, FLG_EQU);
  // Probe on undriven
  DipSwitch dipswitch_1 (
    .sw1(dipswitch_1_sw8[7]), .sw2(dipswitch_1_sw8[6]), .sw3(dipswitch_1_sw8[5]), .sw4(dipswitch_1_sw8[4]),
    .sw5(dipswitch_1_sw8[3]), .sw6(dipswitch_1_sw8[2]), .sw7(dipswitch_1_sw8[1]), .sw8(dipswitch_1_sw8[0]));
  DipSwitch dipswitch_2 (
    .sw1(dipswitch_2_sw8[7]), .sw2(dipswitch_2_sw8[6]), .sw3(dipswitch_2_sw8[5]), .sw4(dipswitch_2_sw8[4]),
    .sw5(dipswitch_2_sw8[3]), .sw6(dipswitch_2_sw8[2]), .sw7(dipswitch_2_sw8[1]), .sw8(dipswitch_2_sw8[0]));
  Pull_Resistor pull_resistor_3 (.node(EXT_0));
  Pull_Resistor pull_resistor_4 (.node(EXT_1));
  Pull_Resistor pull_resistor_5 (.node(pull_resistor_5_node));
  not not_5 (pull_resistor_5_node, EXT_1);
  Multiplexer #(.width(4)) multiplexer_2 (.in0(4'b1110), .in1(MCC_OP), .out(multiplexer_2_out), .sel(not_6_out));
  Pull_Resistor pull_resistor_6 (.node(pull_resistor_6_node));
  Multiplexer #(.select(4)) multiplexer_3 (
    .in0(1'b1), .in1(1'b0), .in2(FLG_ZER), .in3(FLG_CAR), .in4(not_2_out), .in5(not_3_out), .in6(FLG_GRE),
    .in7(FLG_EQU), .in8(FLG_LES), .in9(not_4_out), .in10(EXT_0), .in11(EXT_1), .in12(pull_resistor_5_node),
    .out(pull_resistor_6_node), .sel(MCC_OP));  // open: in13, in14, in15
  not not_6 (not_6_out, or_5_out);
  or or_5 (or_5_out, REG_PC_LO, REG_ALU, REG_SHI, REG_PC_HI, REG_DIP, PRT_C_B, PRT_D_B);
  Pull_Resistor pull_resistor_7 (.node(IF_RES));
  not not_7 (not_7_out, pull_resistor_6_node);
  assign IF_RES = REQ_IF ? not_7_out : 1'bz;  // Controlled_Buffer controlled_buffer_13
  // Probe on ALU
  alu_flags alu_flags_1 (
    .CLK(CLK), .EN(ALU_ACC), .INP(ACC), .SEL(MCC_OP), .SHI(SHI), .GRE(FLG_GRE), .EQU(FLG_EQU), .LES(FLG_LES),
    .ZER(FLG_ZER), .RES(ALU), .CAR(FLG_CAR));
  Multiplexer #(.select(4), .width(8)) multiplexer_4 (
    .in0(dipswitch_1_sw8), .in1(dipswitch_2_sw8), .out(DIP), .sel(MCC_OP));  // open: in2, in3, in4, in5, in6, in7, in8, in9, in10, in11, in12, in13, in14, in15
  regs regs_1 (
    .EN(REG_EN), .CLK(CLK), .VAL(controlled_buffer_5_out), .RGS(multiplexer_2_out), .WRT(regs_1_wrt),
    .REGA(ACC));
  // Probe on ACC
  // Shift_Register #(.length(2), .width(8)) shift_register_1: pin names not known; wires that end beside it: PRT_B_B, CLK, ACC, EXT_MEM_OPERAND, EXT_MEM_OPCODE
  T_Flip_Flop t_ff_1 (.T(PRT_B_B), .clk(CLK), .Qn(EXT_MEM_CLK));  // open: Q, reset, preset
  RAM #(.addrWidth(15), .asyncread("true")) ram_1 (
    .addr(MEM15), .we(and_2_out), .oe(PC_HI[7]), .clk(and_2_out), .din(ACC), .dout(ram_1_dout));
  and and_2 (and_2_out, PC_HI[7], regs_1_wrt);
  not not_8 (not_8_out, CLK);
  and and_3 (EXT_MEM_PRO, not_8_out, EXT_MEM_CLK);
  Counter #(.max('hffff), .width(16)) counter_2 (
    .load(or_7_out), .D(multiplexer_5_out), .count(or_6_out), .Q({PC_HI[7], MEM15}), .clk(CLK), .clr(RST));  // open: carry, up
  or or_6 (or_6_out, INC_PC, or_7_out);
  ROM #(.addrWidth(15)) rom_2 (.addr(MEM15), .data(rom_2_data));
  // Probe on MEM
  assign MEM = PC_HI[7] ? ram_1_dout : 8'bz;  // Controlled_Buffer controlled_buffer_14
  or or_7 (or_7_out, PC_HI_ACC, PC_LO_ACC);
  Comparator comparator_2 (.a(EXT_MEM_OPCODE), .b({8{1'b0}}), .eq(comparator_2_eq));  // open: gt, lt
  Comparator comparator_3 (.a(EXT_MEM_OPCODE), .b(8'h1), .eq(comparator_3_eq));  // open: gt, lt
  Comparator comparator_4 (.a(EXT_MEM_OPCODE), .b(8'h2), .eq(comparator_4_eq));  // open: gt, lt
  Comparator comparator_5 (.a(EXT_MEM_OPCODE), .b(8'h3), .eq(comparator_5_eq));  // open: gt, lt
  Comparator comparator_6 (.a(EXT_MEM_OPCODE), .b(8'h4), .eq(comparator_6_eq));  // open: gt, lt
  Multiplexer #(.width(8)) multiplexer_5 (.in0(MEM15[7:0]), .in1(ACC), .out(multiplexer_5_out[7:0]), .sel(PC_LO_ACC));
  Multiplexer #(.width(8)) multiplexer_6 (
    .in0({PC_HI[7], MEM15[14:8]}), .in1(ACC), .out(multiplexer_5_out[15:8]), .sel(PC_HI_ACC));
  Register register_1 (.D(EXT_MEM_OPERAND), .en(comparator_2_eq), .clk(EXT_MEM_PRO), .Q(register_1_q));  // open: clr
  Register register_2 (.D(EXT_MEM_OPERAND), .en(comparator_3_eq), .clk(EXT_MEM_PRO), .Q(register_2_q));  // open: clr
  Register register_3 (.D(EXT_MEM_OPERAND), .en(comparator_4_eq), .clk(EXT_MEM_PRO), .Q(register_3_q));  // open: clr
  TTL_manager ttl_manager_1 (
    .ACC(ACC), .RST(RST), .EN(PRT_A_B), .TTL_DAT(ttl_manager_1_ttl_dat), .TTL_RST(ttl_manager_1_ttl_rst),
    .TTL_EN(ttl_manager_1_ttl_en));
  not not_9 (not_9_out, PC_HI[7]);
  TTY #(.cols(75), .rows(24)) tty_1 (
    .data(ttl_manager_1_ttl_dat), .clk(CLK), .we(ttl_manager_1_ttl_en), .clr(ttl_manager_1_ttl_rst));
  // Probe on MEM
  assign MEM = not_9_out ? rom_2_data : 8'bz;  // Controlled_Buffer controlled_buffer_15
  RAM #(.addrWidth(17), .asyncread("true"), .\type ("nonvolatile")) ram_2 (
    .addr({register_3_q[0], register_2_q, register_1_q}), .we(comparator_5_eq), .oe(1'b1), .clk(EXT_MEM_PRO),
    .din(EXT_MEM_OPERAND), .dout(ram_2_dout));
  and and_4 (and_4_out, CLK, comparator_6_eq);
  Random random_1 (.next(1'b1), .clk(and_4_out), .out(random_1_out));  // open: clr
  Multiplexer #(.width(8)) multiplexer_7 (
    .in0(ram_2_dout), .in1(random_1_out), .out(multiplexer_7_out), .sel(comparator_6_eq));
  Button button_1 (.out(RST));
  // DipSwitch #(.number(1)) dipswitch_3: pin names not known; wires that end beside it: PRT_BC_SEL
  assign PRT_C = not_10_out ? multiplexer_7_out : 8'bz;  // Controlled_Buffer controlled_buffer_16
  not not_10 (not_10_out, PRT_BC_SEL);
  // Probe on PRT_C
  Keyboard keyboard_1 (
    .clk(key_manager_1_con), .re(key_manager_1_rd), .clr(key_manager_1_clr), .avail(keyboard_1_avail),
    .data(keyboard_1_data));
  KEY_MANAGER key_manager_1 (
    .KEY(keyboard_1_data), .ENABLE(PRT_D_B), .CLK(CLK), .AV(keyboard_1_avail), .OPERAND(MCC_OP),
    .CON(key_manager_1_con), .RD(key_manager_1_rd), .CLR(key_manager_1_clr), .GET(PRT_D), .EXT(EXT_1));

  // Other names for the same wires on the sheet: PC_LO[7:0] = MEM15[7:0]; PC_HI[6:0] = MEM15[14:8]

  // Notes on the sheet:
  //   contents of rom_1 (hex, n*v repeats v):
  //   a0 1 c0 2 ff 0 0 0 3 e0 b0 3 e0 d0 a0 1 c0 2 ff 0 e4 b0 e5 d0 80 1 60 2 0 f0 a0 1 c0 2 3 ff e4 b0 e5
  //   d0 80 1 60 2 20 f0 a0 1 c0 2 3 ff e4 b0 e5 d0 80 1 60 2 40 f0 a0 1 c0 2 3 ff 3 e0 10 3 ff 0 0 0 3 e0
  //   30 3 ff 0 0 0 3 e0 50 3 ff 0 0 0 3 e0 70 3 ff 0 0 0 3 e0 90 3 ff 0 0 0 3 e0 b0 3 ff 0 0 0 3 e0 d0 3
  //   ff 11*0 e4 b0 e5 d0 80 1 60 2 e0 10 a0 1 c0 2 3 ff e4 b0 e5 d0 80 1 60 2 e0 30 a0 1 c0 2 3 ff e4 b0
  //   e5 d0 80 1 60 2 e0 50 a0 1 c0 2 3 ff e4 b0 e5 d0 80 1 60 2 e0 70 a0 1 c0 2 3 ff e4 b0 e5 d0 80 1 60
  //   2 e0 90 a0 1 c0 2 3 ff e4 b0 e5 d0 80 1 60 2 e0 b0 a0 1 c0 2 3 ff e4 b0 e5 d0 80 1 60 2 e0 d0 a0 1
  //   c0 2 3 ff 5*0 30 3 ff 0 50 3 ff 0 70 3 ff 0 90 3 ff 0 b0 3 ff 0 d0 3 ff 20 10 3 ff 20 50 3 ff 20 70
  //   3 ff 20 90 3 ff 20 b0 3 ff 20 d0 3 ff 40 10 3 ff 40 30 3 ff 40 70 3 ff 40 90 3 ff 40 b0 3 ff 40 d0 3
  //   ff 60 10 3 ff 60 30 3 ff 60 50 3 ff 60 90 3 ff 60 b0 3 ff 60 d0 3 ff 80 10 3 ff 80 30 3 ff 80 50 3
  //   ff 80 70 3 ff 80 b0 3 ff 80 d0 3 ff a0 10 3 ff a0 30 3 ff a0 50 3 ff a0 70 3 ff a0 90 3 ff a0 d0 3
  //   ff c0 10 3 ff c0 30 3 ff c0 50 3 ff c0 70 3 ff c0 90 3 ff c0 b0 3 ff 0 48 3 ff 20 48 3 ff 40 48 3 ff
  //   60 48 3 ff 80 48 3 ff a0 48 3 ff c0 48 3 ff 5*0 88 3 ff 20 88 3 ff 40 88 3 ff 60 88 3 ff 80 88 3 ff
  //   a0 88 3 ff c0 88 3 ff 4*0 e7 10 3 ff e7 30 3 ff e7 50 3 ff e7 70 3 ff e7 90 3 ff e7 b0 3 ff e7 d0 3
  //   ff 4*0 38 3 ff 0 28 3 ff 0 18 3 ff 0 8 3 ff 0 3 9 3 ff 3 19 3 ff 3 29 3 ff 3 39 3 ff 3 49 3 ff 3 59
  //   63 ff 3 69 3 ff 3 79 3 ff 3 89 3 ff 3 99 3 ff 3 a9 3 ff 3 b9 3 ff 3 c9 3 ff 3 d9 3 ff 3 e9 3 ff 3 f9
  //   3 ff 0 a 3 ff 20 a 3 ff 40 a 3 ff 60 a 3 ff 80 a 3 ff a0 a 3 ff c0 a 3 ff fa 3 ff 0 eb 10 3 ff eb 30
  //   3 ff eb 50 3 ff eb 70 3 ff eb 90 3 ff eb b0 3 ff eb d0 3 ff 4*0 e4 b0 e5 d0 3 e0 b0 3 e0 2 0 f0 a0 1
  //   c0 2 3 ff 0 0 e4 b0 e5 d0 3 e0 1 3 e0 2 20 f0 a0 1 c0 2 3 ff 10*0 e4 b0 e5 d0 3 e0 1 3 e0 2 40 f0 a0
  //   1 c0 2 3 ff 0 0 e4 b0 e5 d0 3 e0 1 3 e0 2 60 f0 a0 1 c0 2 3 ff 10*0 e4 b0 e5 d0 3 e0 1 3 e0 2 80 f0
  //   a0 1 c0 2 3 ff 0 0 e4 b0 e5 d0 3 e0 1 3 e0 2 a0 f0 a0 1 c0 2 3 ff 10*0 e4 b0 e5 d0 3 e0 1 3 e0 2 c0
  //   f0 a0 1 c0 2 3 ff 6*0 3 e0 48 3 ff 0 0 0 3 e0 88 3 ff 4*0 c 3 ff 20 c 3 ff 40 c 3 ff 60 c 3 ff 80 c
  //   3 ff a0 c 3 ff c0 c 3 ff 4*0 ed 10 3 ff ed 30 3 ff ed 50 3 ff ed 70 3 ff ed 90 3 ff ed b0 3 ff ed d0
  //   3 ff 4*0 ee 10 3 ff ee 30 3 ff ee 50 3 ff ee 70 3 ff ee 90 3 ff ee b0 3 ff ee d0 3 ff 4*0 1f 3 ff 0
  //   3 ff 34*0 43 72 65 61 74 65 64 20 62 79 20 4c 6f 75 69 73 20 57 68 69 74 65 20 32 30 32 36 a 19*0 ff
  //   contents of rom_2 (hex, n*v repeats v):
  //   13 3e 95 19 80 17 0 1b 0 1d b 8f 0 e2 13 a 68 71 1b 0 1d 30 8d 0 94 51 58 19 4 40 21 46 4d 5 13 1 69
  //   73 80 7b 2 0 7 5*0 13 a 5 95 13 0 19 80 17 1 21 19 80 17 0 25 17 10 69 73 82 79 68 71 80 78 3f 19 80
  //   17 3 21 19 80 17 2 25 17 10 69 73 82 79 68 71 80 78 19 80 17 4 3e 21 68 1b a 75 1b 1 1d 50 8d 0 1b
  //   2c 75 1b 1 1d 80 8d 0 1b 2e 75 1b 2 1d 70 8d 0 1b 3a 75 1b 3 1d 70 8d 0 1b 3f 75 1b 3 1d b0 8d 0 1b
  //   52 75 1b 4 1d a0 8d 0 1b 50 75 1b 3 1d d0 8d 0 1b 24 75 1b 5 1d d0 8d 0 2 5 60 15*0 1b 24 75 1b 5 1d
  //   0 8d 0 2 38*0 74 11 1 68 80 7c 2 1 ec 7*0 74 11 1 68 80 7c 2 2 dc 7*0 11 65 94 2 1 10 58*0 46 4d 21
  //   2d 6b 13 0 71 9f 19 3 21 94 13 4 71 9f 19 3 21 94 13 a 95 95 2 6*0 4d 46 2 1 de 11*0 19 81 17 1 9 19
  //   81 17 0 d 2 1 90 0 0 0 13 a 95 13 0 19 80 17 6 21 19 80 17 5 25 17 10 69 73 82 79 68 71 80 78 3f 19
  //   80 17 8 21 19 80 17 7 25 17 10 69 73 82 79 68 71 80 78 19 80 17 4 3e 21 68 1b a 75 19 81 17 3 9 19
  //   81 17 2 d 19 81 17 0 25 19 81 17 1 29 47 4c 21 94 11 1 68 73 80 7b 1b 0 1d f0 89 0 58 51 19 81 17 3
  //   21 68 71 1b 1 1d 70 8b 0 2 2 10 18*0 19 81 17 2 21 68 72 1b 1 1d 70 8b 0 13 a 95 2 15*0 19 81 17 2
  //   21 68 72 1b 2 1d 60 8b 0 13 a 95 2 31*0 4d 46 2 2 ce 11*0 19 81 17 1 9 19 81 17 0 d 2 2 80 0 0 0 13
  //   a 95 13 0 19 80 17 6 21 19 80 17 5 25 17 10 69 73 82 79 68 71 80 78 3f 19 80 17 8 21 19 80 17 7 25
  //   17 10 69 73 82 79 68 71 80 78 19 80 17 4 3e 21 68 1b a 75 19 81 17 3 9 19 81 17 2 d 19 81 17 0 25 19
  //   81 17 1 29 47 4c 21 2 3 10 11 1 68 73 80 7b 1b 1 1d 0 89 0 58 51 19 81 17 3 21 68 71 1b 2 1d 60 8b 0
  //   2 2 30 16*0 30 31 32 33 34 35 36 37 38 39 61 62 63 64 65 66 51 58 68 1d 0 76 9f 19 3 21 94 1d 4 76
  //   9f 19 3 21 94 4d 46 11 20 94 2 2 d2 23*0 4d 46 94 2 2 d2 40*0 19 81 17 0 9 19 81 17 1 d 19 80 17 6
  //   21 19 80 17 5 25 17 10 69 73 82 79 68 71 80 78 19 81 17 1 25 17 0 29 47 4c 5 2 22*0 19 80 17 5 11 0
  //   5 17 6 11 9 5 17 7 11 7 5 17 0 11 0 5 13 0 15 6 2 1 80 0 0 0 19 80 17 5 21 68 1b 4 1d a 76 1d c0 8d
  //   0 1d b 76 1d d0 8d 0 1d c 76 1d e0 8d 0 1d d 76 1 f0 8d 0 2 12*0 1 2 3 4 5 6 7 8 9 a b c d e f 10 11
  //   12 13 14 15 16 17 18 19 1a 1b 1c 1d 1e 1f 20 21 22 23 24 25 26 27 28 29 2a 2b 2c 2d 2e 2f 0 1 2 3 4
  //   5 6 7 8 9 3a b c d e 3f 40 a b c d e f 47 48 49 4a 4b 4c 4d 4e 4f 50 51 52 53 54 55 56 57 58 59 5a
  //   5b 5c 5d 5e 5f 60 a b c d e f 67 68 49 6a 6b 6c 6d 6e 6f 70 50 52 73 74 75 76 77 78 79 7a 7b 7c 7d
  //   7e 7f 80 81 82 83 84 85 86 87 88 89 8a 8b 8c 8d 8e 8f 90 91 92 93 94 95 96 97 98 99 9a 9b 9c 9d 9e
  //   9f 49 4e 30*0 46 4d 21 94 2 11*0 46 4d 21 d2 2 11*0 46 4d da 5 2 11*0 46 4d e2 5 2 11*0 17 0 4d 21
  //   47 5 11 ff 68 73 1b 5 1d 40 8d 0 1b 1 6d 73 80 7b 11 4 6b 70 9c 68 1b f 75 1b 5 1d 2 8b 0 11 2a 94 2
  //   5 2 21*0 11 a 94 94 2 27*0 11 a 94 11 27 94 19 80 17 4 21 94 11 27 94 2 5 80 14*0 19 80 17 5 11 0 5
  //   17 6 11 5 5 17 7 11 d 5 17 0 11 0 5 13 a0 15 5 2 1 80 5*0 69 73 20 6e 6f 74 20 61 20 72 65 63 6f 67
  //   6e 69 73 65 64 20 6f 70 65 72 61 74 6f 72 a 3f 53 59 4e 54 41 58 20 45 52 52 4f 52 a 0 0 0 19 80 17
  //   5 21 68 11 49 70 1b 5 1d 0 8d 0 11 c 70 1b 9 1d a0 8d 0 11 b 70 1b a 1d 0 8d 0 2 14*0 20 20 2d 2d 42
  //   6f 78 4d 6f 6e 69 74 6f 72 20 66 75 6e 63 74 69 6f 6e 73 2d 2d a 63 6f 64 65 6*20 7c 20 66 75 6e 63
  //   74 69 6f 6e 13*20 7c 20 64 65 73 63 72 69 70 74 69 6f 6e a 70*5f a 4*78 6*20 7c 20 72 65 74 75 72 6e
  //   20 6d 65 6d 11*20 7c 20 50 72 69 6e 74 73 20 6d 65 6d 6f 72 79 20 61 64 64 72 20 4*78 a 4*78 2e 4*78
  //   20 7c 20 72 65 74 75 72 6e 20 72 61 6e 67 65 9*20 7c 20 50 72 69 6e 74 73 20 68 65 78 20 72 61 6e 67
  //   65 20 6f 66 20 4*78 20 74 6f 20 4*78 a 4*78 2c 4*78 20 7c 20 72 65 74 75 72 6e 20 61 73 63 69 69 20
  //   72 61 6e 67 65 20 20 20 7c 20 50 72 69 6e 74 73 20 61 73 63 69 69 20 72 61 6e 67 65 20 6f 66 20 4*78
  //   20 74 6f 20 4*78 a 4*78 3a 5*20 7c 20 73 65 74 20 6d 65 6d 14*20 7c 20 57 72 69 74 65 73 20 68 65 78
  //   20 74 6f 20 6d 65 6d 6f 72 79 20 61 64 64 72 20 4*78 a 4*78 52 5*20 7c 20 72 75 6e 20 70 72 6f 67
  //   13*20 7c 20 4a 75 6d 70 73 20 74 6f 20 70 72 6f 67 72 61 6d 20 61 74 20 4*78 a 4*78 50 41 4*20 7c 20
  //   73 65 74 20 70 6f 72 74 20 41 11*20 7c 20 4d 65 6d 6f 72 79 20 61 64 64 72 20 4*78 20 69 6e 74 6f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
endmodule

module regs (
  input  EN,
  input  CLK,
  input  [7:0] VAL,
  input  [3:0] RGS,
  output WRT,
  output [7:0] REGA
);

  wire and_1_out, and_2_out, button_1_out, decoder_1_out0, decoder_1_out1, decoder_1_out2, decoder_1_out3,
       decoder_1_out4, decoder_1_out5, decoder_1_out6, not_1_out;
  wire [7:0] multiplexer_1_out, register_1_q, register_2_q, register_3_q, register_4_q, register_5_q,
       register_6_q, register_7_q;

  and and_1 (and_1_out, EN, RGS[0]);
  Decoder #(.select(3)) decoder_1 (
    .out0(decoder_1_out0), .out1(decoder_1_out1), .out2(decoder_1_out2), .out3(decoder_1_out3),
    .out4(decoder_1_out4), .out5(decoder_1_out5), .out6(decoder_1_out6), .out7(WRT), .sel(RGS[3:1]),
    .en(and_1_out));
  Register register_1 (.D(REGA), .en(decoder_1_out0), .clk(CLK), .Q(register_1_q), .clr(button_1_out));
  Register register_2 (.D(REGA), .en(decoder_1_out1), .clk(CLK), .Q(register_2_q), .clr(button_1_out));
  Register register_3 (.D(REGA), .en(decoder_1_out2), .clk(CLK), .Q(register_3_q), .clr(button_1_out));
  Register register_4 (.D(REGA), .en(decoder_1_out3), .clk(CLK), .Q(register_4_q), .clr(button_1_out));
  Register register_5 (.D(REGA), .en(decoder_1_out4), .clk(CLK), .Q(register_5_q), .clr(button_1_out));
  Register register_6 (.D(REGA), .en(decoder_1_out5), .clk(CLK), .Q(register_6_q), .clr(button_1_out));
  Register register_7 (.D(REGA), .en(decoder_1_out6), .clk(CLK), .Q(register_7_q), .clr(button_1_out));
  Multiplexer #(.select(3), .width(8)) multiplexer_1 (
    .in0(register_1_q), .in1(register_2_q), .in2(register_3_q), .in3(register_4_q), .in4(register_5_q),
    .in5(register_6_q), .in6(register_7_q), .in7(VAL), .out(multiplexer_1_out), .sel(RGS[3:1]));
  Button button_1 (.out(button_1_out));
  not not_1 (not_1_out, RGS[0]);
  and and_2 (and_2_out, EN, not_1_out);
  Register register_8 (.D(multiplexer_1_out), .en(and_2_out), .clk(CLK), .Q(REGA), .clr(button_1_out));

  // Other names for the same wires on the sheet: DAT[2:0] = RGS[3:1]
endmodule

module alu_flags (
  input  CLK,
  input  EN,
  input  [7:0] INP,
  input  [3:0] SEL,
  output [7:0] SHI,
  output GRE,
  output EQU,
  output LES,
  output ZER,
  output [7:0] RES,
  output CAR
);

  wire adder_1_cout, and_1_out, and_2_out, decoder_1_out1, decoder_1_out2, decoder_2_out0, decoder_2_out1,
       decoder_2_out2, decoder_2_out3, not_1_out, not_2_out, not_3_out, not_4_out, not_5_out, not_6_out,
       not_7_out, not_8_out, or_1_out, or_2_out, subtractor_1_bout;
  wire [1:0] SEL_t;
  wire [3:0] shifter_1_out;
  wire [7:0] adder_1_out, divider_1_out, divider_1_rem, IN1, IN2, multiplier_1_cout, multiplier_1_out,
       subtractor_1_out;

  Adder adder_1 (.a(IN1), .b(IN2), .out(adder_1_out), .cout(adder_1_cout));  // open: cin
  assign CAR = decoder_2_out3 ? adder_1_cout : 1'bz;  // Controlled_Buffer controlled_buffer_1
  Decoder #(.select(2)) decoder_1 (
    .out1(decoder_1_out1), .out2(decoder_1_out2), .sel(SEL[3:2]));  // open: out0, out3, en
  Register #(.width(2)) register_1 (.D(SEL[1:0]), .en(EN), .clk(CLK), .Q(SEL_t));  // open: clr
  Decoder #(.select(2)) decoder_2 (
    .out0(decoder_2_out0), .out1(decoder_2_out1), .out2(decoder_2_out2), .out3(decoder_2_out3), .sel(SEL_t));  // open: en
  Subtractor subtractor_1 (.a(IN1), .b(IN2), .out(subtractor_1_out), .bout(subtractor_1_bout));  // open: bin
  assign CAR = decoder_2_out2 ? subtractor_1_bout : 1'bz;  // Controlled_Buffer controlled_buffer_2
  Register register_2 (.D(INP), .en(decoder_1_out1), .clk(and_1_out), .Q(IN1));  // open: clr
  and and_1 (and_1_out, CLK, EN);
  // Probe on IN1
  Multiplier multiplier_1 (.a(IN1), .b(IN2), .out(multiplier_1_out), .cout(multiplier_1_cout));  // open: cin
  or or_1 (or_1_out, multiplier_1_cout[7], multiplier_1_cout[6], multiplier_1_cout[5], multiplier_1_cout[4], multiplier_1_cout[3], multiplier_1_cout[2], multiplier_1_cout[1], multiplier_1_cout[0]);
  assign CAR = decoder_2_out1 ? or_1_out : 1'bz;  // Controlled_Buffer controlled_buffer_3
  Pull_Resistor pull_resistor_1 (.node(CAR));
  Register register_3 (.D(INP), .en(decoder_1_out2), .clk(and_2_out), .Q(IN2));  // open: clr
  and and_2 (and_2_out, CLK, EN);
  Divider divider_1 (.a(IN1), .b(IN2), .out(divider_1_out), .rem(divider_1_rem));  // open: upper
  or or_2 (or_2_out, divider_1_rem[7], divider_1_rem[6], divider_1_rem[5], divider_1_rem[4], divider_1_rem[3], divider_1_rem[2], divider_1_rem[1], divider_1_rem[0]);
  assign CAR = decoder_2_out0 ? or_2_out : 1'bz;  // Controlled_Buffer controlled_buffer_4
  // Probe on IN2
  Pull_Resistor pull_resistor_2 (.node(GRE));
  Pull_Resistor pull_resistor_3 (.node(EQU));
  Comparator #(.mode("unsigned")) comparator_1 (.a(IN2), .b(IN1), .gt(GRE), .eq(EQU), .lt(LES));
  not not_1 (not_1_out, RES[4]);
  not not_2 (not_2_out, RES[5]);
  not not_3 (not_3_out, RES[6]);
  not not_4 (not_4_out, RES[7]);
  Multiplexer #(.select(2), .width(8)) multiplexer_1 (
    .in0(divider_1_out), .in1(multiplier_1_out), .in2(subtractor_1_out), .in3(adder_1_out), .out(RES),
    .sel(SEL_t));
  Pull_Resistor pull_resistor_4 (.node(LES));
  Shifter shifter_1 (.in(IN1), .\dist (IN2[2:0]), .out({SHI[3:0], shifter_1_out}));
  not not_5 (not_5_out, RES[0]);
  not not_6 (not_6_out, RES[1]);
  not not_7 (not_7_out, RES[2]);
  not not_8 (not_8_out, RES[3]);
  and and_3 (ZER, not_5_out, not_6_out, not_7_out, not_8_out, not_1_out, not_2_out, not_3_out, not_4_out);

  assign SHI[7:4] = 4'b0000;

  // Other names for the same wires on the sheet: V1[7:0] = INP
endmodule

module TTL_manager (
  input  [7:0] ACC,
  input  RST,
  input  EN,
  output [6:0] TTL_DAT,
  output TTL_RST,
  output TTL_EN
);

  wire and_1_out, comparator_1_eq;

  Comparator comparator_1 (.a(ACC), .b(8'hc), .eq(comparator_1_eq));  // open: gt, lt
  and and_1 (and_1_out, comparator_1_eq, EN);
  or or_1 (TTL_RST, and_1_out, RST);

  assign TTL_DAT = ACC[6:0];
  assign TTL_EN = EN;
endmodule

module KEY_MANAGER (
  input  [6:0] KEY,
  input  ENABLE,
  input  CLK,
  input  AV,
  input  [3:0] OPERAND,
  output CON,
  output RD,
  output CLR,
  output [7:0] GET,
  output EXT
);

  wire comparator_1_eq;

  and and_1 (CLR, ENABLE, comparator_1_eq);
  Comparator #(.mode("unsigned"), .width(4)) comparator_1 (
    .a(OPERAND), .b(4'b0001), .eq(comparator_1_eq));  // open: gt, lt

  assign CON = CLK;
  assign EXT = AV;
  assign GET = {1'b0, KEY};
  assign RD = ENABLE;
endmodule
